// Logisim project BlinkLED_simulation.circ as structural Verilog: 1 circuit, main circuit main
module main (
  input  [3:0] Reference
);

  wire clock_1_out, comparator_1_eq, counter_1_q, j_k_ff_1_q;
  wire [3:0] counter_2_q;

  Counter #(.max('h1), .width(1)) counter_1 (
    .Q(counter_1_q), .clk(clock_1_out));  // open: load, D, count, carry, up, clr
  Clock clock_1 (.out(clock_1_out));
  LED led_1 (.in(counter_1_q));
  Counter #(.max('hf), .width(4)) counter_2 (
    .Q(counter_2_q), .clk(clock_1_out), .clr(comparator_1_eq));  // open: load, D, count, carry, up
  Comparator #(.width(4)) comparator_1 (.a(counter_2_q), .b(Reference), .eq(comparator_1_eq));  // open: gt, lt
  J_K_Flip_Flop j_k_ff_1 (.J(1'b1), .K(1'b1), .clk(comparator_1_eq), .Q(j_k_ff_1_q));  // open: Qn, preset, reset
  LED led_2 (.in(j_k_ff_1_q));

  // Notes on the sheet:
  //   Count
  //   Reset
  //   Comparator
  //   Memory Element
endmodule
